// Digital circuit Lab02.dig as structural Verilog
module Lab02 (
  input  B,
  input  C,
  input  A,
  input  D,
  output Fa,
  output Fb,
  output Fc,
  output Fd,
  output Fe,
  output Fg,
  output Ff
);

  wire and_1_out, and_2_out, and_3_out, and_4_out, and_5_out, and_6_out, and_7_out, and_8_out, and_9_out,
       and_10_out, and_11_out, and_12_out, and_13_out, and_14_out, and_15_out, and_16_out, and_17_out,
       and_18_out, and_19_out, and_20_out, and_21_out, and_22_out, and_23_out, and_24_out, and_25_out,
       and_26_out, and_27_out, and_28_out, and_29_out, and_30_out, and_31_out, and_32_out, and_33_out,
       not_1_out, not_2_out, not_3_out, not_4_out, not_5_out, not_6_out, not_7_out, not_8_out, not_9_out,
       not_10_out, not_11_out, not_12_out, not_13_out, not_14_out, not_15_out, not_16_out, not_17_out,
       not_18_out, not_19_out, not_20_out, not_21_out, not_22_out, not_23_out, not_24_out;

  Seven_Seg seven_seg_1 (.a(Fa), .b(Fb), .c(Fc), .d(Fd), .e(Fe), .f(Ff), .g(Fg), .dp(1'b0));
  not not_1 (not_1_out, A);
  not not_2 (not_2_out, B);
  not not_3 (not_3_out, C);
  not not_4 (not_4_out, D);
  not not_5 (not_5_out, A);
  not not_6 (not_6_out, B);
  not not_7 (not_7_out, C);
  not not_8 (not_8_out, D);
  not not_9 (not_9_out, A);
  not not_10 (not_10_out, B);
  not not_11 (not_11_out, C);
  and and_1 (and_1_out, not_1_out, C);
  and and_2 (and_2_out, B, C);
  and and_3 (and_3_out, not_2_out, not_4_out);
  and and_4 (and_4_out, not_1_out, B, D);
  and and_5 (and_5_out, not_5_out, not_7_out, not_8_out);
  and and_6 (and_6_out, not_6_out, not_7_out);
  and and_7 (and_7_out, not_6_out, not_8_out);
  and and_8 (and_8_out, not_5_out, C, D);
  and and_9 (and_9_out, A, not_7_out, D);
  and and_10 (and_10_out, not_9_out, B);
  and and_11 (and_11_out, not_10_out, A);
  and and_12 (and_12_out, not_11_out, D);
  and and_13 (and_13_out, not_9_out, not_11_out);
  and and_14 (and_14_out, D, not_9_out);
  and and_15 (and_15_out, A, not_2_out, not_3_out);
  or or_1 (Fa, and_1_out, and_2_out, and_3_out, and_4_out, and_15_out);
  or or_2 (Fb, and_5_out, and_6_out, and_7_out, and_8_out, and_9_out);
  or or_3 (Fc, and_10_out, and_11_out, and_12_out, and_13_out, and_14_out);
  not not_12 (not_12_out, A);
  not not_13 (not_13_out, B);
  not not_14 (not_14_out, C);
  not not_15 (not_15_out, D);
  not not_16 (not_16_out, B);
  not not_17 (not_17_out, D);
  not not_18 (not_18_out, A);
  not not_19 (not_19_out, B);
  not not_20 (not_20_out, D);
  not not_21 (not_21_out, C);
  not not_22 (not_22_out, D);
  not not_23 (not_23_out, C);
  not not_24 (not_24_out, B);
  and and_16 (and_16_out, A, not_14_out);
  and and_17 (and_17_out, B, C, not_15_out);
  and and_18 (and_18_out, not_13_out, C, D);
  and and_19 (and_19_out, not_12_out, not_13_out, not_15_out);
  and and_20 (and_20_out, B, not_14_out, D);
  and and_21 (and_21_out, A, B);
  and and_22 (and_22_out, C, not_17_out);
  and and_23 (and_23_out, C, A);
  and and_24 (and_24_out, not_17_out, A);
  and and_25 (and_25_out, not_16_out, not_17_out);
  and and_26 (and_26_out, A, not_19_out);
  and and_27 (and_27_out, A, C);
  and and_28 (and_28_out, not_18_out, B, not_21_out);
  and and_29 (and_29_out, not_18_out, not_21_out, not_22_out);
  and and_30 (and_30_out, B, C, not_22_out);
  and and_31 (and_31_out, C, not_20_out);
  and and_32 (and_32_out, B, not_23_out);
  and and_33 (and_33_out, not_24_out, C);
  or or_4 (Fd, and_16_out, and_17_out, and_18_out, and_19_out, and_20_out);
  or or_5 (Fe, and_21_out, and_22_out, and_23_out, and_24_out, and_25_out);
  or or_6 (Ff, and_26_out, and_27_out, and_28_out, and_29_out, and_30_out);
  or or_7 (Fg, A, and_31_out, and_32_out, and_33_out);

  // Other names for the same wires on the sheet: A_a = A; A_b = A; A_c = A; A_d = A; A_e = A; A_f = A; A_g = A;
  //   B_a = B; B_b = B; B_c = B; B_d = B; B_e = B; B_f = B; B_g = B; C_a = C; C_b = C; C_c = C; C_d = C; C_e = C;
  //   C_f = C; C_g = C; D_a = D; D_b = D; D_c = D; D_d = D; D_e = D; D_f = D; D_g = D
endmodule
