// Digital circuit register-file.dig as structural Verilog
module register_file (
  input  [4:0] ReadReg1,
  input  [4:0] ReadReg2,
  input  [4:0] WriteReg,
  input  [31:0] WriteData,
  input  RegWrite,
  input  Clock,
  output [31:0] ReadData1,
  output [31:0] ReadData2
);

  wire _0, _1, _2, _3, _4, _5, _6, _7, _8, _9, _10, _11, _12, _13, _14, _15, _16, _17, _18, _19, _20, _21,
       _22, _23, _24, _25, _26, _27, _28, _29, _30, _31;
  wire [4:0] and_1_out, bitextender_1_out;
  wire [31:0] Q_0, Q_1, Q_2, Q_3, Q_4, Q_5, Q_6, Q_7, Q_8, Q_9, Q_10, Q_11, Q_12, Q_13, Q_14, Q_15, Q_16,
       Q_17, Q_18, Q_19, Q_20, Q_21, Q_22, Q_23, Q_24, Q_25, Q_26, Q_27, Q_28, Q_29, Q_30, Q_31;

  BitExtender #(.inputBits(1), .outputBits(5)) bitextender_1 (.in(RegWrite), .out(bitextender_1_out));
  assign and_1_out = WriteReg & bitextender_1_out;  // And and_1, 5 bits wide
  Decoder #(.Selector_Bits(5)) decoder_1 (
    .sel(and_1_out), .out_0(_0), .out_1(_1), .out_2(_2), .out_3(_3), .out_4(_4), .out_5(_5), .out_6(_6),
    .out_7(_7), .out_8(_8), .out_9(_9), .out_10(_10), .out_11(_11), .out_12(_12), .out_13(_13), .out_14(_14),
    .out_15(_15), .out_16(_16), .out_17(_17), .out_18(_18), .out_19(_19), .out_20(_20), .out_21(_21),
    .out_22(_22), .out_23(_23), .out_24(_24), .out_25(_25), .out_26(_26), .out_27(_27), .out_28(_28),
    .out_29(_29), .out_30(_30), .out_31(_31));
  Register #(.Bits(32)) Register_0 (.D({32{1'b0}}), .C(Clock), .en(_0), .Q(Q_0));
  Register #(.Bits(32)) Register_8 (.D(WriteData), .C(Clock), .en(_8), .Q(Q_8));
  Register #(.Bits(32)) Register_16 (.D(WriteData), .C(Clock), .en(_16), .Q(Q_16));
  Register #(.Bits(32)) Register_24 (.D(WriteData), .C(Clock), .en(_24), .Q(Q_24));
  Register #(.Bits(32)) Register_1 (.D(WriteData), .C(Clock), .en(_1), .Q(Q_1));
  Register #(.Bits(32)) Register_9 (.D(WriteData), .C(Clock), .en(_9), .Q(Q_9));
  Register #(.Bits(32)) Register_17 (.D(WriteData), .C(Clock), .en(_17), .Q(Q_17));
  Register #(.Bits(32)) Register_25 (.D(WriteData), .C(Clock), .en(_25), .Q(Q_25));
  Register #(.Bits(32)) Register_2 (.D(WriteData), .C(Clock), .en(_2), .Q(Q_2));
  Register #(.Bits(32)) Register_10 (.D(WriteData), .C(Clock), .en(_10), .Q(Q_10));
  Register #(.Bits(32)) Register_18 (.D(WriteData), .C(Clock), .en(_18), .Q(Q_18));
  Register #(.Bits(32)) Register_26 (.D(WriteData), .C(Clock), .en(_26), .Q(Q_26));
  Register #(.Bits(32)) Register_3 (.D(WriteData), .C(Clock), .en(_3), .Q(Q_3));
  Register #(.Bits(32)) Register_11 (.D(WriteData), .C(Clock), .en(_11), .Q(Q_11));
  Register #(.Bits(32)) Register_19 (.D(WriteData), .C(Clock), .en(_19), .Q(Q_19));
  Register #(.Bits(32)) Register_27 (.D(WriteData), .C(Clock), .en(_27), .Q(Q_27));
  Register #(.Bits(32)) Register_4 (.D(WriteData), .C(Clock), .en(_4), .Q(Q_4));
  Register #(.Bits(32)) Register_12 (.D(WriteData), .C(Clock), .en(_12), .Q(Q_12));
  Register #(.Bits(32)) Register_20 (.D(WriteData), .C(Clock), .en(_20), .Q(Q_20));
  Register #(.Bits(32)) Register_28 (.D(WriteData), .C(Clock), .en(_28), .Q(Q_28));
  Register #(.Bits(32)) Register_5 (.D(WriteData), .C(Clock), .en(_5), .Q(Q_5));
  Register #(.Bits(32)) Register_13 (.D(WriteData), .C(Clock), .en(_13), .Q(Q_13));
  Register #(.Bits(32)) Register_21 (.D(WriteData), .C(Clock), .en(_21), .Q(Q_21));
  Register #(.Bits(32)) Register_29 (.D(WriteData), .C(Clock), .en(_29), .Q(Q_29));
  Register #(.Bits(32)) Register_6 (.D(WriteData), .C(Clock), .en(_6), .Q(Q_6));
  Register #(.Bits(32)) Register_14 (.D(WriteData), .C(Clock), .en(_14), .Q(Q_14));
  Register #(.Bits(32)) Register_22 (.D(WriteData), .C(Clock), .en(_22), .Q(Q_22));
  Register #(.Bits(32)) Register_30 (.D(WriteData), .C(Clock), .en(_30), .Q(Q_30));
  Register #(.Bits(32)) Register_7 (.D(WriteData), .C(Clock), .en(_7), .Q(Q_7));
  Register #(.Bits(32)) Register_15 (.D(WriteData), .C(Clock), .en(_15), .Q(Q_15));
  Register #(.Bits(32)) Register_23 (.D(WriteData), .C(Clock), .en(_23), .Q(Q_23));
  Register #(.Bits(32)) Register_31 (.D(WriteData), .C(Clock), .en(_31), .Q(Q_31));
  Multiplexer #(.Bits(32), .Selector_Bits(5)) multiplexer_1 (
    .sel(ReadReg1), .in_0(Q_0), .in_1(Q_1), .in_2(Q_2), .in_3(Q_3), .in_4(Q_4), .in_5(Q_5), .in_6(Q_6),
    .in_7(Q_7), .in_8(Q_8), .in_9(Q_9), .in_10(Q_10), .in_11(Q_11), .in_12(Q_12), .in_13(Q_13), .in_14(Q_14),
    .in_15(Q_15), .in_16(Q_16), .in_17(Q_17), .in_18(Q_18), .in_19(Q_19), .in_20(Q_20), .in_21(Q_21),
    .in_22(Q_22), .in_23(Q_23), .in_24(Q_24), .in_25(Q_25), .in_26(Q_26), .in_27(Q_27), .in_28(Q_28),
    .in_29(Q_29), .in_30(Q_30), .in_31(Q_31), .out(ReadData1));
  Multiplexer #(.Selector_Bits(5), .Bits(32)) multiplexer_2 (
    .sel(ReadReg2), .in_0(Q_0), .in_1(Q_1), .in_2(Q_2), .in_3(Q_3), .in_4(Q_4), .in_5(Q_5), .in_6(Q_6),
    .in_7(Q_7), .in_8(Q_8), .in_9(Q_9), .in_10(Q_10), .in_11(Q_11), .in_12(Q_12), .in_13(Q_13), .in_14(Q_14),
    .in_15(Q_15), .in_16(Q_16), .in_17(Q_17), .in_18(Q_18), .in_19(Q_19), .in_20(Q_20), .in_21(Q_21),
    .in_22(Q_22), .in_23(Q_23), .in_24(Q_24), .in_25(Q_25), .in_26(Q_26), .in_27(Q_27), .in_28(Q_28),
    .in_29(Q_29), .in_30(Q_30), .in_31(Q_31), .out(ReadData2));

  // Other names for the same wires on the sheet: RD1[31:0] = ReadData1; RD2[31:0] = ReadData2
endmodule

/* Test case Register File Test:
WriteReg WriteData RegWrite Clock ReadReg1 ReadReg2 ReadData1 ReadData2

# $1 = 25
1 25 1 C 1 0 25 0

# $2 = 30
2 30 1 C 0 2 0 30

# $(N+1) = (N+1)
loop(N, 30)
	(N+1) (N+1) 1 C (N+1) (N) (N+1) (N)
end loop

# $(N+1) = N-60
loop(N, 30)
	(N+1) (N-60) 1 C (N+1) (N+1) (N-60) (N-60)
end loop

# Try writing to $0. This should not write anything
0 25 1 C 0 0 0 0

# try writing when RegWrite = 0
# (the registers should still have their old values)
loop(N, 30)
	(N+1) (N+80) 0 C (N+1) (N+1) (N-60) (N-60)
end loop
*/
